# Fritzing sketch Solenoid_Valve (saved by Fritzing 0.9.1b)
breadboards: 1

parts:
  Part1 = Arduino Pro Mini v13
  TIP122 = TRANSISTOR_NPN [package=to-92-ammo]
  D1 = Rectifier Diode [part_number=1N4001 package="300 mil [THT]"]
  R1 = Resistor [tolerance=±5% resistance=220 package=THT]
  M1 = DC Motor
  R2 = Resistor [tolerance=±5% resistance=220 package=THT]
  R3 = Resistor [tolerance=±5% resistance=220 package=THT]

nets:
  GND: Part1.GND, TIP122.E, R3.Pin_0
  N1: Part1.VCC, D1.cathode, M1.pin_1, R2.Pin_1
  N2: Part1.A0, R2.Pin_0, R3.Pin_1
  N3: Part1.D4, R1.Pin_0
  N4: TIP122.B, D1.anode, M1.pin_2
  N5: TIP122.C, R1.Pin_1
