# Fritzing sketch Voltage_Divider (saved by Fritzing 0.9.1b)
breadboards: 1

parts:
  Part1 = Arduino Pro Mini v13
  R1 = Resistor [tolerance=±5% resistance=220 package=THT]
  R2 = Resistor [tolerance=±5% resistance=100 package=THT]

nets:
  N1: Part1.VCC, R1.Pin_1
  N2: Part1.A0, R1.Pin_0, R2.Pin_1
  N3: Part1.GND, R2.Pin_0
